# Fritzing sketch robomodo (saved by Fritzing 0.8.7b)

parts:
  Composant1 = Arduino Fio (Funnel I/O)
  VCC1 = Battery  # not connected
  J1 = Basic Servo
  J2 = Basic Servo

nets:
  VCC: Composant1.VCC, J1.vcc, J2.vcc
  GND: Composant1.GND, J1.gnd, J2.gnd
  N1: Composant1.D3_PWM, J2.pulse
  N2: Composant1.D5_PWM, J1.pulse
